# Fritzing sketch Simulacion (saved by Fritzing 1.0.5)
breadboards: 1

parts:
  Componente1 = Arduino Uno (Rev3) - ICSP
  Keypad4x2 = Keypad Membran 4x4
  R1 = Resistor [tolerance=±5% power=0.25W resistance=220 package=THT]
  R2 = Resistor [tolerance=±5% power=0.25W resistance=220 package=THT]
  R3 = Resistor [tolerance=±5% power=0.25W resistance=220 package=THT]
  LED1 = RGB LED (com. cathode, rgb) [color="Red (633nm)" current=0.030A package="5 mm [THT]"]
  Grove1 = Grove OLED 128x96

nets:
  N1: Componente1.A0, Keypad4x2.Pin8
  N2: Componente1.A4/SDA, Grove1.SDA
  N3: Componente1.A5/SCL, Grove1.SCL
  N4: Componente1.D8, Keypad4x2.Pin1
  N5: Componente1.D9_PWM, R3.Pin_0
  N6: Componente1.D10_PWM/SS, R2.Pin_0
  N7: Componente1.D11_PWM/MOSI, R1.Pin_0
  GND: Componente1.GND, LED1.common_cathode, Grove1.GND
  N8: Componente1.D2, Keypad4x2.Pin7
  N9: Componente1.D3_PWM, Keypad4x2.Pin6
  N10: Componente1.D4, Keypad4x2.Pin5
  N11: Componente1.D5_PWM, Keypad4x2.Pin4
  N12: Componente1.D6_PWM, Keypad4x2.Pin3
  N13: Componente1.D7, Keypad4x2.Pin2
  5V: Componente1.5V, Grove1.VCC
  N14: R1.Pin_1, LED1.red_anode
  N15: R2.Pin_1, LED1.green_anode
  N16: R3.Pin_1, LED1.blue_anode

custom parts:
  Keypad Membran 4x4: Membrane Keypad 4x4 Matrix
