# Fritzing sketch simulacion (saved by Fritzing 1.0.5)
breadboards: 1

parts:
  S1 = Round Pushbutton
  S2 = Round Pushbutton
  R1 = Resistor [tolerance=±5% power=0.25W resistance=10k package=THT]
  R2 = Resistor [tolerance=±5% power=0.25W resistance=10k package=THT]
  LED1 = LED - 5mm [color="Red (633nm)" current=0.030A package="5 mm [THT]"]
  R3 = Resistor [tolerance=±5% power=0.25W resistance=220 package=THT]
  Componente1 = Arduino Uno (Rev3)

nets:
  N1: S1.leg0, R1.Pin_1, Componente1.D2
  N2: S1.leg1, S2.leg1, Componente1.5V
  N3: S2.leg0, R2.Pin_1, Componente1.D3_PWM
  N4: R1.Pin_0, R2.Pin_0, LED1.cathode, Componente1.GND
  N5: LED1.anode, R3.Pin_0
  N6: R3.Pin_1, Componente1.D9_PWM
